// Logisim project practica5.circ as structural Verilog: 5 circuits, main circuit Ejercicio1
module Ejercicio1 (
);


  // Notes on the sheet:
  //   Automata Simulator
endmodule

module Ejercicio2 (
  input  Clock_in,
  input  [7:0] in_2,
  output [7:0] out_3
);

  D_Flip_Flop d_ff_1 (.clk(Clock_in), .D(in_2[0]), .Q(out_3[0]));  // open: Qn, preset, en, reset
  D_Flip_Flop d_ff_2 (.clk(Clock_in), .D(in_2[1]), .Q(out_3[1]));  // open: Qn, preset, en, reset
  D_Flip_Flop d_ff_3 (.clk(Clock_in), .D(in_2[2]), .Q(out_3[2]));  // open: Qn, preset, en, reset
  D_Flip_Flop d_ff_4 (.clk(Clock_in), .D(in_2[3]), .Q(out_3[3]));  // open: Qn, preset, en, reset
  D_Flip_Flop d_ff_5 (.clk(Clock_in), .D(in_2[4]), .Q(out_3[4]));  // open: Qn, preset, en, reset
  D_Flip_Flop d_ff_6 (.clk(Clock_in), .D(in_2[5]), .Q(out_3[5]));  // open: Qn, preset, en, reset
  D_Flip_Flop d_ff_7 (.clk(Clock_in), .D(in_2[6]), .Q(out_3[6]));  // open: Qn, preset, en, reset
  D_Flip_Flop d_ff_8 (.clk(Clock_in), .D(in_2[7]), .Q(out_3[7]));  // open: Qn, preset, en, reset

  // Notes on the sheet:
  //   8-Bit Register
  //   Register_in
endmodule

module Ejercicio3 (
  input  Register_in,
  output [7:0] out_2
);

  wire clock_1_out;

  Clock clock_1 (.out(clock_1_out));
  D_Flip_Flop d_ff_1 (.clk(clock_1_out), .D(Register_in), .Q(out_2[0]));  // open: Qn, preset, en, reset
  D_Flip_Flop d_ff_2 (.clk(clock_1_out), .D(out_2[0]), .Q(out_2[1]));  // open: Qn, preset, en, reset
  D_Flip_Flop d_ff_3 (.clk(clock_1_out), .D(out_2[1]), .Q(out_2[2]));  // open: Qn, preset, en, reset
  D_Flip_Flop d_ff_4 (.clk(clock_1_out), .D(out_2[2]), .Q(out_2[3]));  // open: Qn, preset, en, reset
  D_Flip_Flop d_ff_5 (.clk(clock_1_out), .D(out_2[3]), .Q(out_2[4]));  // open: Qn, preset, en, reset
  D_Flip_Flop d_ff_6 (.clk(clock_1_out), .D(out_2[4]), .Q(out_2[5]));  // open: Qn, preset, en, reset
  D_Flip_Flop d_ff_7 (.clk(clock_1_out), .D(out_2[5]), .Q(out_2[6]));  // open: Qn, preset, en, reset
  D_Flip_Flop d_ff_8 (.clk(clock_1_out), .D(out_2[6]), .Q(out_2[7]));  // open: Qn, preset, en, reset

  // Notes on the sheet:
  //   Clock_in
  //   Shift Register Simulator
endmodule

module Ejercicio4 (
  input  [1:0] in_1,
  input  [7:0] Inmediato,
  input  [1:0] Guardar_Registro,
  input  [1:0] in_4,
  output [7:0] Leer_Datos_1,
  output [7:0] Leer_Datos_2
);

  wire clock_1_out;
  wire [7:0] demultiplexer_1_out0, demultiplexer_1_out1, demultiplexer_1_out2, demultiplexer_1_out3,
       ejercicio2_1_out_3, ejercicio2_2_out_3, ejercicio2_3_out_3, ejercicio2_4_out_3;

  Clock clock_1 (.out(clock_1_out));
  Demultiplexer #(.select(2), .width(8)) demultiplexer_1 (
    .out0(demultiplexer_1_out0), .out1(demultiplexer_1_out1), .out2(demultiplexer_1_out2),
    .out3(demultiplexer_1_out3), .in(Inmediato), .sel(Guardar_Registro));  // open: en
  Ejercicio2 ejercicio2_1 (.Clock_in(clock_1_out), .in_2(demultiplexer_1_out0), .out_3(ejercicio2_1_out_3));
  Ejercicio2 ejercicio2_2 (.Clock_in(clock_1_out), .in_2(demultiplexer_1_out1), .out_3(ejercicio2_2_out_3));
  Ejercicio2 ejercicio2_3 (.Clock_in(clock_1_out), .in_2(demultiplexer_1_out2), .out_3(ejercicio2_3_out_3));
  Ejercicio2 ejercicio2_4 (.Clock_in(clock_1_out), .in_2(demultiplexer_1_out3), .out_3(ejercicio2_4_out_3));
  Multiplexer #(.select(2), .width(8)) multiplexer_1 (
    .in0(ejercicio2_1_out_3), .in1(ejercicio2_2_out_3), .in2(ejercicio2_3_out_3), .in3(ejercicio2_4_out_3),
    .out(Leer_Datos_1), .sel(in_1));  // open: en
  Multiplexer #(.select(2), .width(8)) multiplexer_2 (
    .in0(ejercicio2_1_out_3), .in1(ejercicio2_2_out_3), .in2(ejercicio2_3_out_3), .in3(ejercicio2_4_out_3),
    .out(Leer_Datos_2), .sel(in_4));  // open: en

  // Notes on the sheet:
  //   Register Bank
  //   Clock_in
  //   Seleccionar Registro 1
  //   Seleccionar Registro 2
endmodule

module Ejercicio5 (
);


  // Notes on the sheet:
  //   Adder/Substractor
endmodule
